# Fritzing sketch Sonar (saved by Fritzing 0.9.0b)
breadboards: 1

parts:
  LED1 = smd LED [color="Red (633nm)" package="0603 [SMD]"]
  R1 = Resistor [tolerance=±5% resistance=330 package="0805 [SMD]"]
  U1 = HC-SR04 [chip_label=IC package="SIP (Single Inline) [THT]"]
  J1 = Basic Servo
  Part1 = Arduino Uno (Rev3)

nets:
  GND: LED1.cathode, U1.GND, J1.gnd, Part1.GND
  N1: LED1.anode, R1.Pin_0
  N2: R1.Pin_1, Part1.D8
  VCC: U1.Vcc, J1.vcc, Part1.5V
  N3: U1.Trig, Part1.D10_PWM/SS
  N4: U1.Echo, Part1.D11_PWM/MOSI
  N5: J1.pulse, Part1.D12/MISO

custom parts:
  HC-SR04: HC-SR04 ultrasound distance sensor
